# Fritzing sketch WiringDiagram (saved by Fritzing 1.0.4)

parts:
  Part1 = Arduino Mega ADK (Rev3)
  J8 = Basic Servo
  J9 = Basic Servo
  J10 = Basic Servo
  J12 = Basic Servo
  Part3 = Adafruit PCA9685 PWM/Servo Breakout [part_number=815]
  TB6600 = IC, SIP package, 12 pins [chip_label=TB6600]
  M1 = Stepper Motor - Bipolar
  J4 = Basic Servo
  J3 = Basic Servo
  J13 = Basic Servo
  J14 = Basic Servo
  J15 = Basic Servo
  J16 = Basic Servo
  J17 = Basic Servo
  J18 = Basic Servo
  Part4 = Adafruit PCA9685 PWM/Servo Breakout [part_number=815]
  J19 = Power Jack [package=power_jack_slot]
  DC1 = DC_DC_SZBK07 [package=board_screw]
  A1 = XY-3606
  TB6601 = IC, SIP package, 12 pins [chip_label=TB6600]
  M2 = Stepper Motor - Bipolar
  TB6602 = IC, SIP package, 12 pins [chip_label=TB6600]
  M3 = Stepper Motor - Bipolar
  TB6603 = IC, SIP package, 12 pins [chip_label=TB6600]
  TB6604 = IC, SIP package, 12 pins [chip_label=TB6600]
  TB6605 = IC, SIP package, 12 pins [chip_label=TB6600]
  M4 = Stepper Motor - Bipolar
  M5 = Stepper Motor - Bipolar
  M6 = Stepper Motor - Bipolar
  KW12-3 = JL012-13-5.2 Lever (Limit) Switch SPDT + NO + NC [part_number=JL012-13-5.2]
  KW12-3_2 = JL012-13-5.2 Lever (Limit) Switch SPDT + NO + NC [part_number=JL012-13-5.2]
  KW12-3_3 = JL012-13-5.2 Lever (Limit) Switch SPDT + NO + NC [part_number=JL012-13-5.2]
  KW12-3_4 = JL012-13-5.2 Lever (Limit) Switch SPDT + NO + NC [part_number=JL012-13-5.2]
  KW12-3_5 = JL012-13-5.2 Lever (Limit) Switch SPDT + NO + NC [part_number=JL012-13-5.2]
  KW12-3_6 = JL012-13-5.2 Lever (Limit) Switch SPDT + NO + NC [part_number=JL012-13-5.2]

nets (from the schematic view):
  N1: Part1.A0, Part3.SCL
  N2: Part1.A1, Part3.SDA
  N3: Part1.A2, Part4.SCL
  N4: Part1.A3, Part4.SDA
  GND: Part1.GND, TB6600.pin11, J13.gnd, J14.gnd, J15.gnd, J16.gnd, J17.gnd, J18.gnd, Part4.GND, J19.GNDBREAK, DC1.IN-, A1.Pin_2, A1.Pin_3, TB6601.pin11, TB6602.pin11, TB6603.pin11, TB6604.pin11, TB6605.pin11, KW12-3.C, KW12-3_2.C, KW12-3_3.C, KW12-3_4.C, KW12-3_5.C, KW12-3_6.C
  VCC: Part1.5V, Part3.VCC, TB6600.pin2, TB6600.pin4, TB6600.pin6, Part4.VCC, TB6601.pin2, TB6601.pin4, TB6601.pin6, TB6602.pin2, TB6602.pin4, TB6602.pin6, TB6603.pin2, TB6603.pin4, TB6603.pin6, TB6604.pin2, TB6604.pin4, TB6604.pin6, TB6605.pin2, TB6605.pin4, TB6605.pin6
  N5: Part1.D1/TX0, KW12-3_5.NC
  N6: Part1.D2_PWM, KW12-3_4.NC
  N7: Part1.D3_PWM, KW12-3_3.NC
  N8: Part1.D4_PWM, KW12-3_2.NC
  N9: Part1.D5_PWM, KW12-3.NC
  N10: Part1.D6_PWM, KW12-3_6.NC
  N11: Part1.D32, TB6603.pin3
  N12: Part1.D33, TB6603.pin5
  N13: Part1.D34, TB6605.pin3
  N14: Part1.D35, TB6605.pin5
  N15: Part1.D36, TB6604.pin5
  N16: Part1.D37, TB6604.pin3
  N17: Part1.D38, TB6600.pin3
  N18: Part1.D39, TB6600.pin5
  N19: Part1.D44, TB6601.pin5
  N20: Part1.D45, TB6601.pin3
  N21: Part1.D46, TB6602.pin5
  N22: Part1.D47, TB6602.pin3
  GND_2: J8.gnd, J9.gnd, J10.gnd, J12.gnd, Part3.GND, J4.gnd, J3.gnd, DC1.OUT-
  VCC_2: J8.vcc, J9.vcc, J10.vcc, J12.vcc, Part3.PWRIN, J4.vcc, J3.vcc, DC1.OUT+
  N23: J8.pulse, Part3.PWM1
  N24: J9.pulse, Part3.PWM4
  N25: J10.pulse, Part3.PWM5
  N26: J12.pulse, Part3.PWM0
  N27: Part3.PWM3, J3.pulse
  N28: Part3.PWM2, J4.pulse
  N29: TB6600.pin7, M1.D
  N30: TB6600.pin8, M1.B
  N31: TB6600.pin9, M1.C
  N32: TB6600.pin10, M1.A
  N33: TB6600.pin12, J19.PWR, DC1.IN+, A1.Pin_1, TB6601.pin12, TB6602.pin12, TB6603.pin12, TB6604.pin12, TB6605.pin12
  VCC_3: J13.vcc, J14.vcc, J15.vcc, J16.vcc, J17.vcc, J18.vcc, Part4.PWRIN, A1.Pin_4
  N34: J13.pulse, Part4.PWM2
  N35: J14.pulse, Part4.PWM0
  N36: J15.pulse, Part4.PWM4
  N37: J16.pulse, Part4.PWM1
  N38: J17.pulse, Part4.PWM3
  N39: J18.pulse, Part4.PWM5
  N40: TB6601.pin7, M2.D
  N41: TB6601.pin8, M2.B
  N42: TB6601.pin9, M2.C
  N43: TB6601.pin10, M2.A
  N44: TB6602.pin7, M3.D
  N45: TB6602.pin8, M3.B
  N46: TB6602.pin9, M3.C
  N47: TB6602.pin10, M3.A
  N48: TB6603.pin7, M6.D
  N49: TB6603.pin8, M6.B
  N50: TB6603.pin9, M6.C
  N51: TB6603.pin10, M6.A
  N52: TB6604.pin7, M5.D
  N53: TB6604.pin8, M5.B
  N54: TB6604.pin9, M5.C
  N55: TB6604.pin10, M5.A
  N56: TB6605.pin7, M4.D
  N57: TB6605.pin8, M4.B
  N58: TB6605.pin9, M4.C
  N59: TB6605.pin10, M4.A

custom parts:
  Adafruit PCA9685 PWM/Servo Breakout: Using only two pins, control 16 free-running PWM outputs! I2C-controlled PWM driver with a built in clock. Unlike the TLC5940 family, you do not need to continuously send it signal tying up your microcontroller, its completely free running! 5V compliant, which means you can control it from a 3.3V microcontroller and still safely drive up to 6V outputs (this is good for when you want to control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
  DC_DC_SZBK07: DC-DC Converter step down voltage regulator SZBK07 custom sketch.
  XY-3606: 24V/12V turn 5V 5A power module, DC-DC XY-3606 Power Converter Super LM2596S.
  JL012-13-5.2 Lever (Limit) Switch SPDT + NO + NC: Micro Switch; Model No.: JL012-13.5-2; Actuator Action: Momentary; Actuator Type: Hinge Lever; Contact Configuration: 1NO, 1NC (SPDT) Temperature -25~65℃；Relative humidity: below 85%; Rate Voltage: 125V AC; Rated Current: 1A.
